# Fritzing sketch Simon (saved by Fritzing 0.9.3b)
breadboards: 1

parts:
  R2 = Resistor [tolerance=±5% resistance=220 package=THT]
  R3 = Resistor [tolerance=±5% resistance=220 package=THT]
  R4 = Resistor [tolerance=±5% resistance=330 package=THT]
  S1 = Pushbutton [package="[THT]"]
  S2 = Pushbutton [package="[THT]"]
  S3 = Pushbutton [package="[THT]"]
  S4 = Pushbutton [package="[THT]"]
  R5 = Resistor [tolerance=±5% resistance=10k package=THT]
  Composant1 = Arduino Uno (Rev3)
  R6 = Resistor [tolerance=±5% resistance=220 package=THT]
  R7 = Resistor [tolerance=±5% resistance=220 package=THT]
  R8 = Resistor [tolerance=±5% resistance=220 package=THT]
  R9 = Resistor [tolerance=±5% resistance=220 package=THT]
  LED2 = LED - 5mm [color="Blue (430nm)" package="5 mm [THT]"]
  LED3 = LED - 5mm [color="Yellow (585nm)" package="5 mm [THT]"]
  LED4 = LED - 5mm [color="Green (555nm)" package="5 mm [THT]"]
  LED1 = LED - 5mm [color="Red (633nm)" package="5 mm [THT]"]
  J1 = Piezo Speaker

nets:
  N1: R2.Pin_0, R2.Pin_1, R3.Pin_0, R3.Pin_1, R4.Pin_0, R4.Pin_1, S1.Pin_1, S1.Pin_2, S1.Pin_3, S1.Pin_4, S2.Pin_1, S2.Pin_2, S2.Pin_3, S2.Pin_4, S3.Pin_1, S3.Pin_2, S3.Pin_3, S3.Pin_4, S4.Pin_1, S4.Pin_2, S4.Pin_3, S4.Pin_4, R5.Pin_1, Composant1.A0, Composant1.5V
  N2: R5.Pin_0, Composant1.GND, R6.Pin_1, R7.Pin_1, R8.Pin_1, R9.Pin_1, J1.pin1
  N3: Composant1.D8, J1.pin2
  N4: Composant1.D2, LED4.anode
  N5: Composant1.D3_PWM, LED3.anode
  N6: Composant1.D4, LED2.anode
  N7: Composant1.D5_PWM, LED1.anode
  N8: R6.Pin_0, LED4.cathode
  N9: R7.Pin_0, LED3.cathode
  N10: R8.Pin_0, LED2.cathode
  N11: R9.Pin_0, LED1.cathode
