# Fritzing sketch simon2 (saved by Fritzing 0.9.3b)
circuit board: 6.49286cm x 5.59157cm
perfboards: 1

parts:
  Composant1 = Arduino Nano (Rev3.0)
  R2 = Resistor [tolerance=±5% resistance=220 package=THT]
  R3 = Resistor [tolerance=±5% resistance=220 package=THT]
  R4 = Resistor [tolerance=±5% resistance=220 package=THT]
  R6 = Resistor [tolerance=±5% resistance=220 package=THT]
  R7 = Resistor [tolerance=±5% resistance=220 package=THT]
  R8 = Resistor [tolerance=±1% resistance=10k package=THT]
  LED2 = LED - 5mm [color="Red (633nm)" package="5 mm [THT]"]
  LED3 = LED - 5mm [color="Red (633nm)" package="5 mm [THT]"]
  LED4 = LED - 5mm [color="Red (633nm)" package="5 mm [THT]"]
  R5 = Resistor [tolerance=±5% resistance=220 package=THT]
  J2 = female pin header, 4 pins [form="♀ (female)"]
  LED1 = LED - 5mm [color="Red (633nm)" package="5 mm [THT]"]
  R1 = Resistor [tolerance=±5% resistance=220 package=THT]
  S6 = Pushbutton [package=THT]
  S7 = Pushbutton [package=THT]
  S8 = Pushbutton [package=THT]
  S9 = Pushbutton [package=THT]

nets:
  N1: Composant1.GND, R8.Pin_0, LED2.cathode, LED3.cathode, LED4.cathode, J2.pin4, LED1.cathode
  N2: Composant1.D2, R1.Pin_0
  N3: Composant1.D3, R2.Pin_0
  N4: Composant1.D4, R3.Pin_0
  N5: Composant1.D5, R4.Pin_0
  N6: Composant1.D8, J2.pin1
  N7: Composant1.5V, S6.leg0, S7.leg0, S8.leg0, S9.leg0
  N8: Composant1.A0, R8.Pin_1, R5.Pin_1, S6.leg1
  N9: R2.Pin_1, LED2.anode
  N10: R3.Pin_1, LED3.anode
  N11: R4.Pin_1, LED4.anode
  N12: R6.Pin_0, R7.Pin_1, S8.leg1
  N13: R6.Pin_1, R5.Pin_0, S7.leg1
  N14: R7.Pin_0, S9.leg1
  N15: LED1.anode, R1.Pin_1
